# Fritzing sketch EM robotic ploter (saved by Fritzing 0.9.9b)
breadboards: 1

parts:
  part = Arduino Uno (Rev3) - ICSP
  J1 = Basic Servo
  J2 = Basic Servo
  J3 = Basic Servo
  part_2 = Thumb Joystick
  Power_plug1 = Power plug

nets:
  N1: part.A0, part_2.SEL
  N2: part.A1, part_2.HORZ
  N3: part.A2, part_2.VERT
  VCC: part.5V, J1.vcc, J2.vcc, J3.vcc, part_2.VCC, Power_plug1.VCC
  GND: part.GND, J1.gnd, J2.gnd, J3.gnd, part_2.GND, Power_plug1.GND
  N4: part.D9_PWM, J3.pulse
  N5: part.D10_PWM/SS, J2.pulse
  N6: part.D11_PWM/MOSI, J1.pulse
